# Fritzing sketch esqueminha (saved by Fritzing 0.9.4)
breadboards: 2

parts:
  U1 = ESP32-38PinWide [part_number=ESP32-38PinWide]
  microSD1 = MicroSD Card Module
  U2 = TMP36 [package=to-92]
  Componente1 = LCD1602-I2C

nets:
  N1: U1.GPIO27, U2.VOUT
  GND: U1.GPIO11, microSD1.GND, U2.GND, Componente1.GND
  VCC: U1.VIN, microSD1.VCC, U2.VCC, Componente1.VCC
  N2: U1.GPIO5, microSD1.CS
  N3: U1.GPIO18, microSD1.SCK
  N4: U1.GPIO19, microSD1.MISO
  N5: U1.GPIO21, Componente1.SDA
  N6: U1.GPIO22, Componente1.SCL
  N7: U1.GPIO23, microSD1.MOSI

notes:
  Sensor DHT:
  GND = GND
  VCC = 3,3 V ou 5 V
  DATA = 27
  Modulo SD Card.
  VCC = Vin
  GND = GND
  CS = 5
  SCK = 18
  MOSI = 23
  MISO= 19
  Display 16x2 I2C
  GND = GND
  VCC = VIN
  SDA = 21
  SCL = 22

custom parts:
  ESP32-38PinWide: Generic 38-Pin ESP32 with wide format (only access to one side of pins on a breadboard) based on Stephen Lilley's HiLetgo ESP-WROOM-32 ESP32 ESP-32S Development Board.
  LCD1602-I2C: A standard character display, usually with 2x16 characters. Comes in many colors with LCM1602 IIC attached.
